// Logisim project cpu.circ as structural Verilog: 1 circuit, main circuit cpu
module cpu (
  input  clk,
  input  [31:0] Instruction,
  input  [31:0] MemReadData,
  output [31:0] MemAddress,
  output [31:0] ProgramCounter,
  output [31:0] ra,
  output [31:0] sp,
  output [31:0] t0,
  output [31:0] t1,
  output [31:0] t2,
  output [31:0] s0,
  output [31:0] s1,
  output [31:0] a0,
  output [3:0] MemWriteMask,
  output [31:0] MemWriteData
);

  wire ASel, BrEq, BrLt, BrUn, BSel, MemRW, PCSel, RegWEn;
  wire [1:0] WBSel;
  wire [2:0] ImmSel;
  wire [3:0] ALUSel;
  wire [31:0] DataToReg, IMM, multiplexer_1_out, multiplexer_2_out, multiplexer_3_out, PCplus4, RegData1,
       RegData2, WriteBack;

  Adder #(.width(32)) adder_1 (.a(ProgramCounter), .b(32'h4), .out(PCplus4));  // open: cin, cout
  Register #(.width(32)) PC (.D(multiplexer_1_out), .clk(clk), .Q(ProgramCounter));  // open: en, clr
  Multiplexer #(.width(32)) multiplexer_1 (.in0(PCplus4), .in1(MemAddress), .out(multiplexer_1_out), .sel(PCSel));
  control_logic control_logic_1 (
    .Instruction(Instruction), .BrEq(BrEq), .BrLt(BrLt), .PCSel(PCSel), .RegWEn(RegWEn), .ImmSel(ImmSel),
    .BrUn(BrUn), .ASel(ASel), .BSel(BSel), .ALUSel(ALUSel), .MemWEn(MemRW), .WBSel(WBSel));
  // Probe on RegWEn
  regfile regfile_1 (
    .ReadIndex1(Instruction[19:15]), .ReadIndex2(Instruction[24:20]), .WriteIndex(Instruction[11:7]),
    .WriteData(WriteBack), .RegWEn(RegWEn), .clk(clk), .ra(ra), .sp(sp), .t0(t0), .t1(t1), .t2(t2), .s0(s0),
    .s1(s1), .a0(a0), .ReadData1(RegData1), .ReadData2(RegData2));
  imm_gen imm_gen_1 (.Instruction(Instruction), .ImmSel(ImmSel), .Immediate(IMM));
  // Probe on multiplexer_3_out
  // Probe on multiplexer_2_out
  Multiplexer #(.width(32)) multiplexer_2 (.in0(ProgramCounter), .in1(RegData1), .out(multiplexer_2_out), .sel(ASel));
  Multiplexer #(.width(32)) multiplexer_3 (.in0(IMM), .in1(RegData2), .out(multiplexer_3_out), .sel(BSel));
  alu alu_1 (.A(multiplexer_2_out), .B(multiplexer_3_out), .ALUSel(ALUSel), .ALUResult(MemAddress));
  // Probe on MemAddress
  branch_comp branch_comp_1 (.BrData1(RegData1), .BrData2(RegData2), .BrUn(BrUn), .BrEq(BrEq), .BrLt(BrLt));
  // Probe on RegData2
  // Probe on MemReadData
  partial_store partial_store_1 (
    .Instruction(Instruction), .MemAddress(MemAddress), .DataFromReg(RegData2), .MemRW(MemRW),
    .MemWriteMask(MemWriteMask), .DataToMem(MemWriteData));
  // Probe on MemWriteData
  partial_load partial_load_1 (
    .Instruction(Instruction), .MemAddress(MemAddress), .DataFromMem(MemReadData), .DataToReg(DataToReg));
  // Probe on DataToReg
  // Probe on WBSel
  Multiplexer #(.select(2), .width(32)) multiplexer_4 (
    .in0(DataToReg), .in1(MemAddress), .in2(PCplus4), .out(WriteBack), .sel(WBSel));  // open: in3

  // Other names for the same wires on the sheet: ALUResult[31:0] = MemAddress; opcode[6:0] = Instruction[6:0];
  //   RD[4:0] = Instruction[11:7]; func3[2:0] = Instruction[14:12]; RS1[4:0] = Instruction[19:15];
  //   RS2[4:0] = Instruction[24:20]; func7[6:0] = Instruction[31:25]

  // Notes on the sheet:
  //   To IMEM
  //   IMEM (do **NOT** move this)
  //   From IMEM
  //   Inputs/Outputs for testing. Do **NOT** move these.
  //   It is OK to move the PC, RegFile, ALU, MEM, Branch Comp, Imm Gen, Partial Load, Partial Store and Control Logic to wherever is most convenient for you when constructing your CPU, and to delete this text
  //   To DMEM
  //   DMEM (do **NOT** move this)
  //   From DMEM
endmodule
