// Logisim project imm-gen.circ as structural Verilog: 1 circuit, main circuit imm_gen
module imm_gen (
  input  [31:0] Instruction,
  input  [2:0] ImmSel,
  output [31:0] Immediate
);

  wire [31:0] bit_extender_1_out, bit_extender_2_out, bit_extender_3_out, bit_extender_4_out,
       bit_extender_5_out, bit_extender_6_out;

  assign bit_extender_1_out = {{20{Instruction[31]}}, Instruction[31:20]};  // Bit_Extender bit_extender_1
  assign bit_extender_2_out = {{27{Instruction[24]}}, Instruction[24:20]};  // Bit_Extender bit_extender_2
  assign bit_extender_3_out = {{20{Instruction[31]}}, {Instruction[31:25], Instruction[11:7]}};  // Bit_Extender bit_extender_3
  assign bit_extender_4_out = {{19{Instruction[31]}}, {Instruction[31], Instruction[7], Instruction[30:25], Instruction[11:8], 1'b0}};  // Bit_Extender bit_extender_4
  assign bit_extender_5_out = {{12{Instruction[31]}}, Instruction[31:12]};  // Bit_Extender bit_extender_5
  assign bit_extender_6_out = {{11{Instruction[31]}}, {Instruction[31], Instruction[19:12], Instruction[20], Instruction[30:21], 1'b0}};  // Bit_Extender bit_extender_6
  Demultiplexer #(.select(3), .width(32)) demultiplexer_1 (
    .out0(bit_extender_2_out), .out1(bit_extender_1_out), .out2(bit_extender_3_out),
    .out3(bit_extender_4_out), .out4(bit_extender_5_out), .out5(bit_extender_6_out), .in(Immediate),
    .sel(ImmSel));  // open: out6, out7

  // Notes on the sheet:
  //   INPUTS to your circuit
  //   DON'T CHANGE THE LOCATIONS OF THE INPUTS AND OUTPUTS!
  //   OUTPUT from your circuit
endmodule
